// Logisim project computer.circ as structural Verilog: 11 circuits, main circuit main
module main (
  input  reset
);

  wire frequencydiviser_1_clock_dirac, frequencydiviser_1_clock_instruction,
       instructiondecoder_1_fu_enable_output, instructiondecoder_1_fu_output_alu_or_shifter,
       instructiondecoder_1_ram_enable_read, instructiondecoder_1_ram_enable_write,
       instructiondecoder_1_rf_enable_write, pc_clock_out;
  wire [1:0] instructiondecoder_1_fu_select_shifter;
  wire [3:0] instructiondecoder_1_fu_select_alu;
  wire [4:0] instructiondecoder_1_rf_address_output_a, instructiondecoder_1_rf_address_output_b,
       instructiondecoder_1_rf_address_write;
  wire [7:0] programcounter_1_instruction_pointer;
  wire [15:0] Data_Memory_dout, functionunit_1_output_fu, instructiondecoder_1_ram_address,
       registerfile_1_output_a, registerfile_1_output_b, undriven;
  wire [31:0] Instruction_Memory_data;

  Clock pc_clock (.out(pc_clock_out));
  ProgramCounter programcounter_1 (
    .reset(reset), .increment(frequencydiviser_1_clock_instruction),
    .Instruction_pointer(programcounter_1_instruction_pointer));
  ROM #(.dataWidth(32)) Instruction_Memory (
    .addr(programcounter_1_instruction_pointer), .data(Instruction_Memory_data));
  frequencyDiviser frequencydiviser_1 (
    .clock(pc_clock_out), .clock_dirac(frequencydiviser_1_clock_dirac),
    .clock_instruction(frequencydiviser_1_clock_instruction));
  InstructionDecoder instructiondecoder_1 (
    .Instruction(Instruction_Memory_data[31:26]), .rs(Instruction_Memory_data[25:21]),
    .rt(Instruction_Memory_data[20:16]), .immediate(Instruction_Memory_data[15:0]),
    .RF_enable_write(instructiondecoder_1_rf_enable_write),
    .RF_address_write(instructiondecoder_1_rf_address_write),
    .RF_address_output_A(instructiondecoder_1_rf_address_output_a),
    .RF_address_output_B(instructiondecoder_1_rf_address_output_b),
    .FU_select_alu(instructiondecoder_1_fu_select_alu),
    .FU_select_shifter(instructiondecoder_1_fu_select_shifter),
    .FU_enable_output(instructiondecoder_1_fu_enable_output),
    .FU_output_alu_or_shifter(instructiondecoder_1_fu_output_alu_or_shifter),
    .RAM_enable_write(instructiondecoder_1_ram_enable_write),
    .RAM_enable_read(instructiondecoder_1_ram_enable_read), .RAM_address(instructiondecoder_1_ram_address));  // open: immediate_output, immediate_select
  Multiplexer #(.width(16)) multiplexer_1 (.in1(registerfile_1_output_b));  // open: in0, out, sel
  RegisterFile registerfile_1 (
    .Input_RF(functionunit_1_output_fu), .enable_write(instructiondecoder_1_rf_enable_write),
    .address_write(instructiondecoder_1_rf_address_write),
    .address_output_A(instructiondecoder_1_rf_address_output_a),
    .address_output_B(instructiondecoder_1_rf_address_output_b), .clock(frequencydiviser_1_clock_dirac),
    .Output_A(registerfile_1_output_a), .Output_B(registerfile_1_output_b));
  FunctionUnit functionunit_1 (
    .Input_A(registerfile_1_output_a), .Input_B(undriven), .select_alu(instructiondecoder_1_fu_select_alu),
    .select_shifter(instructiondecoder_1_fu_select_shifter),
    .select_alu_or_shifter(instructiondecoder_1_fu_output_alu_or_shifter),
    .enable_ouput(instructiondecoder_1_fu_enable_output), .Output_FU(functionunit_1_output_fu));  // open: overflow
  assign functionunit_1_output_fu = instructiondecoder_1_ram_enable_read ? Data_Memory_dout : 16'bz;  // Controlled_Buffer controlled_buffer_1
  RAM #(.addrWidth(16), .dataWidth(16)) Data_Memory (
    .addr(instructiondecoder_1_ram_address), .we(instructiondecoder_1_ram_enable_write),
    .oe(instructiondecoder_1_ram_enable_read), .clk(frequencydiviser_1_clock_dirac),
    .din(registerfile_1_output_a), .dout(Data_Memory_dout));

  // Notes on the sheet:
  //   contents of Instruction_Memory (hex, n*v repeats v):
  //   4000000 4010100 2020001 3020300
endmodule

module ram_perso (
  input  [7:0] address,
  input  write_enable,
  input  [7:0] input_word,
  input  in_4,
  output [7:0] output_word
);

  wire clock_1_out, not_1_out;
  wire [7:0] address_register_q, input_register_q, ram_1_dout;

  Clock clock_1 (.out(clock_1_out));
  Register address_register (.D(address), .en(in_4), .clk(clock_1_out), .Q(address_register_q));  // open: clr
  Register input_register (.D(input_word), .en(in_4), .clk(clock_1_out), .Q(input_register_q));  // open: clr
  Register output_register (.D(ram_1_dout), .en(in_4), .clk(clock_1_out), .Q(output_word));  // open: clr
  not not_1 (not_1_out, write_enable);
  RAM ram_1 (
    .addr(address_register_q), .we(write_enable), .oe(not_1_out), .clk(clock_1_out), .din(input_register_q),
    .dout(ram_1_dout));
endmodule

module ALU_AC (
  input  C_in,
  input  [1:0] S,
  input  [15:0] A,
  input  [15:0] B,
  output [15:0] G,
  output C_out
);

  wire and_1_out, and_2_out, and_3_out, and_4_out, and_5_out, and_6_out, and_7_out, and_8_out, and_9_out,
       and_10_out, and_11_out, and_12_out, and_13_out, and_14_out, and_15_out, and_16_out, and_17_out,
       and_18_out, and_19_out, and_20_out, and_21_out, and_22_out, and_23_out, and_24_out, and_25_out,
       and_26_out, and_27_out, and_28_out, and_29_out, and_30_out, and_31_out, and_32_out, not_1_out,
       not_2_out, not_3_out, not_4_out, not_5_out, not_6_out, not_7_out, not_8_out, not_9_out, not_10_out,
       not_11_out, not_12_out, not_13_out, not_14_out, not_15_out, not_16_out;
  wire [15:0] or_1_out;

  not not_1 (not_1_out, B[0]);
  not not_2 (not_2_out, B[1]);
  not not_3 (not_3_out, B[2]);
  not not_4 (not_4_out, B[3]);
  not not_5 (not_5_out, B[4]);
  not not_6 (not_6_out, B[5]);
  not not_7 (not_7_out, B[6]);
  not not_8 (not_8_out, B[7]);
  not not_9 (not_9_out, B[8]);
  not not_10 (not_10_out, B[9]);
  not not_11 (not_11_out, B[10]);
  not not_12 (not_12_out, B[11]);
  not not_13 (not_13_out, B[12]);
  not not_14 (not_14_out, B[13]);
  not not_15 (not_15_out, B[14]);
  not not_16 (not_16_out, B[15]);
  and and_1 (and_1_out, B[0], S[0]);
  and and_2 (and_2_out, not_1_out, S[1]);
  and and_3 (and_3_out, B[1], S[0]);
  and and_4 (and_4_out, not_2_out, S[1]);
  and and_5 (and_5_out, B[2], S[0]);
  and and_6 (and_6_out, not_3_out, S[1]);
  and and_7 (and_7_out, B[3], S[0]);
  and and_8 (and_8_out, not_4_out, S[1]);
  and and_9 (and_9_out, B[4], S[0]);
  and and_10 (and_10_out, not_5_out, S[1]);
  and and_11 (and_11_out, B[5], S[0]);
  and and_12 (and_12_out, not_6_out, S[1]);
  and and_13 (and_13_out, B[6], S[0]);
  and and_14 (and_14_out, not_7_out, S[1]);
  and and_15 (and_15_out, B[7], S[0]);
  and and_16 (and_16_out, not_8_out, S[1]);
  and and_17 (and_17_out, B[8], S[0]);
  and and_18 (and_18_out, not_9_out, S[1]);
  and and_19 (and_19_out, B[9], S[0]);
  and and_20 (and_20_out, not_10_out, S[1]);
  and and_21 (and_21_out, B[10], S[0]);
  and and_22 (and_22_out, not_11_out, S[1]);
  and and_23 (and_23_out, B[11], S[0]);
  and and_24 (and_24_out, not_12_out, S[1]);
  and and_25 (and_25_out, B[12], S[0]);
  and and_26 (and_26_out, not_13_out, S[1]);
  and and_27 (and_27_out, B[13], S[0]);
  and and_28 (and_28_out, not_14_out, S[1]);
  and and_29 (and_29_out, B[14], S[0]);
  and and_30 (and_30_out, not_15_out, S[1]);
  and and_31 (and_31_out, B[15], S[0]);
  and and_32 (and_32_out, not_16_out, S[1]);
  or or_1 (or_1_out[0], and_1_out, and_2_out);
  or or_2 (or_1_out[1], and_3_out, and_4_out);
  or or_3 (or_1_out[2], and_5_out, and_6_out);
  or or_4 (or_1_out[3], and_7_out, and_8_out);
  or or_5 (or_1_out[4], and_9_out, and_10_out);
  or or_6 (or_1_out[5], and_11_out, and_12_out);
  or or_7 (or_1_out[6], and_13_out, and_14_out);
  or or_8 (or_1_out[7], and_15_out, and_16_out);
  or or_9 (or_1_out[8], and_17_out, and_18_out);
  or or_10 (or_1_out[9], and_19_out, and_20_out);
  or or_11 (or_1_out[10], and_21_out, and_22_out);
  or or_12 (or_1_out[11], and_23_out, and_24_out);
  or or_13 (or_1_out[12], and_25_out, and_26_out);
  or or_14 (or_1_out[13], and_27_out, and_28_out);
  or or_15 (or_1_out[14], and_29_out, and_30_out);
  or or_16 (or_1_out[15], and_31_out, and_32_out);
  Adder #(.width(16)) adder_1 (.a(A), .b(or_1_out), .out(G), .cin(C_in), .cout(C_out));
endmodule

module ALU_LC (
  input  [1:0] S,
  input  [15:0] A,
  input  [15:0] B,
  output [15:0] G
);

  wire [15:0] and_1_out, not_1_out, or_1_out, xor_1_out;

  assign and_1_out = A & B;  // AND_Gate and_1, 16 bits wide
  assign or_1_out = A | B;  // OR_Gate or_1, 16 bits wide
  assign xor_1_out = A ^ B;  // XOR_Gate xor_1, 16 bits wide
  assign not_1_out = ~A;  // NOT_Gate not_1, 16 bits wide
  Multiplexer #(.select(2), .width(16)) multiplexer_1 (
    .in0(and_1_out), .in1(or_1_out), .in2(xor_1_out), .in3(not_1_out), .out(G), .sel(S));
endmodule

module ALU (
  input  C_in,
  input  [2:0] S,
  input  [15:0] A,
  input  [15:0] B,
  output C_overflow,
  output [15:0] G
);

  wire [15:0] alu_ac_1_g, alu_lc_1_g;

  ALU_AC alu_ac_1 (.C_in(C_in), .S(S[1:0]), .A(A), .B(B), .G(alu_ac_1_g), .C_out(C_overflow));
  ALU_LC alu_lc_1 (.S(S[1:0]), .A(A), .B(B), .G(alu_lc_1_g));
  Multiplexer #(.width(16)) multiplexer_1 (.in0(alu_ac_1_g), .in1(alu_lc_1_g), .out(G), .sel(S[2]));
endmodule

module Basic_Shifter (
  input  [15:0] A,
  input  Input_Left,
  input  Input_Right,
  input  [1:0] S,
  output [15:0] G
);

  wire undriven, undriven_2, undriven_3, undriven_4, undriven_5, undriven_6, undriven_7, undriven_8,
       undriven_9, undriven_10, undriven_11, undriven_12, undriven_13, undriven_14, undriven_15;

  // NoConnect on undriven
  Multiplexer #(.select(2)) multiplexer_1 (
    .in0(A[15]), .in1(Input_Right), .in2(A[14]), .in3(undriven), .out(G[15]), .sel(S));
  // NoConnect on undriven_2
  Multiplexer #(.select(2)) multiplexer_2 (
    .in0(A[14]), .in1(A[15]), .in2(A[13]), .in3(undriven_2), .out(G[14]), .sel(S));
  // NoConnect on undriven_3
  Multiplexer #(.select(2)) multiplexer_3 (
    .in0(A[13]), .in1(A[14]), .in2(A[12]), .in3(undriven_3), .out(G[13]), .sel(S));
  // NoConnect on undriven_4
  Multiplexer #(.select(2)) multiplexer_4 (
    .in0(A[12]), .in1(A[13]), .in2(A[11]), .in3(undriven_4), .out(G[12]), .sel(S));
  // NoConnect on undriven_5
  Multiplexer #(.select(2)) multiplexer_5 (
    .in0(A[11]), .in1(A[12]), .in2(A[10]), .in3(undriven_5), .out(G[11]), .sel(S));
  // NoConnect on undriven_6
  Multiplexer #(.select(2)) multiplexer_6 (
    .in0(A[10]), .in1(A[11]), .in2(A[9]), .in3(undriven_6), .out(G[10]), .sel(S));
  // NoConnect on undriven_7
  Multiplexer #(.select(2)) multiplexer_7 (.in0(A[9]), .in1(A[10]), .in2(A[8]), .in3(undriven_7), .out(G[9]), .sel(S));
  // NoConnect on undriven_8
  Multiplexer #(.select(2)) multiplexer_8 (.in0(A[8]), .in1(A[9]), .in2(A[9]), .in3(undriven_8), .out(G[8]), .sel(S));
  // NoConnect on undriven_9
  Multiplexer #(.select(2)) multiplexer_9 (.in0(A[9]), .in1(A[8]), .in2(A[6]), .in3(undriven_9), .out(G[7]), .sel(S));
  // NoConnect on undriven_10
  Multiplexer #(.select(2)) multiplexer_10 (.in0(A[6]), .in1(A[9]), .in2(A[5]), .in3(undriven_10), .out(G[6]), .sel(S));
  // NoConnect on undriven_11
  Multiplexer #(.select(2)) multiplexer_11 (.in0(A[5]), .in1(A[6]), .in2(A[4]), .in3(undriven_11), .out(G[5]), .sel(S));
  // NoConnect on undriven_12
  Multiplexer #(.select(2)) multiplexer_12 (.in0(A[4]), .in1(A[5]), .in2(A[3]), .in3(undriven_12), .out(G[4]), .sel(S));
  // NoConnect on undriven_13
  Multiplexer #(.select(2)) multiplexer_13 (.in0(A[3]), .in1(A[4]), .in2(A[2]), .in3(undriven_13), .out(G[3]), .sel(S));
  // NoConnect on undriven_14
  Multiplexer #(.select(2)) multiplexer_14 (.in0(A[2]), .in1(A[3]), .in2(A[1]), .in3(undriven_14), .out(G[2]), .sel(S));
  // NoConnect on undriven_15
  Multiplexer #(.select(2)) multiplexer_15 (.in0(A[1]), .in1(A[2]), .in2(A[0]), .in3(undriven_15), .out(G[1]), .sel(S));
  Multiplexer #(.select(2)) multiplexer_16 (
    .in0(A[0]), .in1(A[1]), .in2(Input_Left), .out(G[0]), .sel(S));  // open: in3

  assign A[7] = A[9];
endmodule

module ProgramCounter (
  input  reset,
  input  increment,
  output [7:0] Instruction_pointer
);

  wire multiplexer_2_out;
  wire [7:0] adder_1_out, multiplexer_1_out;

  Multiplexer #(.width(8)) multiplexer_1 (.in0(adder_1_out), .in1({8{1'b1}}), .out(multiplexer_1_out), .sel(reset));
  Register counter_register (
    .D(multiplexer_1_out), .en(multiplexer_2_out), .clk(multiplexer_2_out), .Q(Instruction_pointer));  // open: clr
  Multiplexer multiplexer_2 (.in0(increment), .in1(reset), .out(multiplexer_2_out), .sel(reset));
  Adder adder_1 (.a(8'h1), .b(Instruction_pointer), .out(adder_1_out));  // open: cin, cout
endmodule

module InstructionDecoder (
  input  [5:0] Instruction,
  input  [4:0] rs,
  input  [4:0] rt,
  input  [15:0] immediate,
  output RF_enable_write,
  output [4:0] RF_address_write,
  output [4:0] RF_address_output_A,
  output [4:0] RF_address_output_B,
  output [3:0] FU_select_alu,
  output [1:0] FU_select_shifter,
  output FU_enable_output,
  output FU_output_alu_or_shifter,
  output RAM_enable_write,
  output RAM_enable_read,
  output [15:0] RAM_address,
  output [15:0] immediate_output,
  output immediate_select
);

  wire and_1_out, and_2_out, decoder_1_out1, undriven, undriven_2, undriven_3, undriven_4, undriven_5;
  wire [4:0] demultiplexer_1_out0, demultiplexer_1_out1;

  Demultiplexer #(.width(5)) demultiplexer_1 (
    .out0(demultiplexer_1_out0), .out1(demultiplexer_1_out1), .in(Instruction[4:0]), .sel(Instruction[5]));
  Decoder #(.select(5)) decoder_1 (
    .out1(decoder_1_out1), .sel(demultiplexer_1_out0), .en(and_1_out));  // open: out0, out2, out3, out4, out5, out6, out7, out8, out9, out10, out11, out12, out13, out14, out15, out16, out17, out18, out19, out20, out21, out22, out23, out24, out25, out26, out27, out28, out29, out30, out31
  and and_1 (and_1_out, 1'b1, ~Instruction[5]);  // AND_Gate
  and and_2 (and_2_out, 1'b1, Instruction[5]);
  Decoder #(.select(5)) decoder_2 (
    .sel(demultiplexer_1_out1), .en(and_2_out));  // open: out0, out1, out2, out3, out4, out5, out6, out7, out8, out9, out10, out11, out12, out13, out14, out15, out16, out17, out18, out19, out20, out21, out22, out23, out24, out25, out26, out27, out28, out29, out30, out31
  or or_1 (RF_enable_write, 1'b0, undriven_5);
  buf or_2 (FU_select_alu[0], 1'b0);  // OR_Gate
  or or_3 (FU_select_alu[1], 1'b0, undriven);
  buf or_4 (FU_select_alu[2], 1'b0);  // OR_Gate
  buf or_5 (FU_select_alu[3], 1'b0);  // OR_Gate
  buf or_6 (FU_select_shifter[0], 1'b0);  // OR_Gate
  buf or_7 (FU_select_shifter[1], 1'b0);  // OR_Gate
  or or_8 (FU_enable_output, 1'b0, undriven_2);
  buf or_9 (FU_output_alu_or_shifter, 1'b0);  // OR_Gate
  or or_10 (RAM_enable_write, 1'b0, undriven_3);
  or or_11 (RAM_enable_read, 1'b0, undriven_4);

  // Notes on the sheet:
  //   register_A
endmodule

module FunctionUnit (
  input  [15:0] Input_A,
  input  [15:0] Input_B,
  input  [3:0] select_alu,
  input  [1:0] select_shifter,
  input  select_alu_or_shifter,
  input  enable_ouput,
  output overflow,
  output [15:0] Output_FU
);

  wire [15:0] alu_1_g, basic_shifter_1_g, multiplexer_1_out;

  ALU alu_1 (.C_in(select_alu[0]), .S(select_alu[3:1]), .A(Input_A), .B(Input_B), .C_overflow(overflow), .G(alu_1_g));
  Basic_Shifter basic_shifter_1 (
    .A(Input_B), .Input_Left(1'b0), .Input_Right(1'b0), .S(select_shifter), .G(basic_shifter_1_g));
  Multiplexer #(.width(16)) multiplexer_1 (
    .in0(alu_1_g), .in1(basic_shifter_1_g), .out(multiplexer_1_out), .sel(select_alu_or_shifter));
  assign Output_FU = enable_ouput ? multiplexer_1_out : 16'bz;  // Controlled_Buffer controlled_buffer_1
endmodule

module RegisterFile (
  input  [15:0] Input_RF,
  input  enable_write,
  input  [4:0] address_write,
  input  [4:0] address_output_A,
  input  [4:0] address_output_B,
  input  clock,
  output [15:0] Output_A,
  output [15:0] Output_B
);

  wire and_1_out, decoder_1_out0, decoder_1_out1, decoder_1_out2, decoder_1_out3;
  wire [15:0] registre_0_q, registre_1_q, registre_2_q, registre_3_q;

  and and_1 (and_1_out, enable_write, clock);
  Decoder #(.select(2)) decoder_1 (
    .out0(decoder_1_out0), .out1(decoder_1_out1), .out2(decoder_1_out2), .out3(decoder_1_out3),
    .sel(address_write[1:0]), .en(and_1_out));
  Register #(.trigger("high"), .width(16)) registre_0 (
    .D(Input_RF), .en(decoder_1_out0), .clk(decoder_1_out0), .Q(registre_0_q));  // open: clr
  Register #(.trigger("high"), .width(16)) registre_1 (
    .D(Input_RF), .en(decoder_1_out1), .clk(decoder_1_out1), .Q(registre_1_q));  // open: clr
  Register #(.trigger("high"), .width(16)) registre_2 (
    .D(Input_RF), .en(decoder_1_out2), .clk(decoder_1_out2), .Q(registre_2_q));  // open: clr
  Register #(.trigger("high"), .width(16)) registre_3 (
    .D(Input_RF), .en(decoder_1_out3), .clk(decoder_1_out3), .Q(registre_3_q));  // open: clr
  Multiplexer #(.select(2), .width(16)) multiplexer_1 (
    .in0(registre_0_q), .in1(registre_1_q), .in2(registre_2_q), .in3(registre_3_q), .out(Output_A),
    .sel(address_output_A[1:0]));
  Multiplexer #(.select(2), .width(16)) multiplexer_2 (
    .in0(registre_0_q), .in1(registre_1_q), .in2(registre_2_q), .in3(registre_3_q), .out(Output_B),
    .sel(address_output_B[1:0]));
endmodule

module frequencyDiviser (
  input  clock,
  output clock_dirac,
  output clock_instruction
);

  not not_1 (clock_dirac, clock);
  D_Flip_Flop d_ff_1 (.D(clock_instruction), .clk(clock), .Qn(clock_instruction));  // open: Q, preset, reset
endmodule
